// Logisim project Carry_Forward_Adder.circ as structural Verilog: 2 circuits, main circuit main
module main (
  input  [3:0] X,
  input  [3:0] in_2,
  input  [3:0] Y,
  input  [3:0] in_4,
  input  in_5,
  input  in_6,
  output S0,
  output S1,
  output out_9,
  output out_10,
  output out_11,
  output out_12,
  output out_13
);

  wire and_1_out, and_2_out, and_3_out, and_4_out, and_5_out, and_6_out, and_7_out, and_8_out, and_9_out,
       and_10_out, and_11_out, and_12_out, and_13_out, and_14_out, and_15_out, and_16_out, and_17_out,
       and_18_out, and_19_out, and_20_out, and_21_out, and_22_out, and_23_out, C1_out, C2_out, c3_out,
       C4_out, or_1_out, or_2_out, or_3_out, or_4_out, or_5_out, p1P2g0_out, p2g1_out, P3P2G1_out, xor_1_out,
       xor_2_out, xor_3_out, xor_5_out, xor_6_out, xor_7_out;

  FULLADDER fulladder_1 (.X(X[1]), .Y(Y[1]), .SUM(S1));  // open: Cin
  FULLADDER fulladder_2 (.X(X[0]), .Y(Y[0]), .Cin(in_5), .SUM(S0));
  xor xor_1 (xor_1_out, X[0], Y[0]);
  and and_1 (and_1_out, X[0], Y[0]);
  xor xor_2 (xor_2_out, X[1], Y[1]);
  and and_2 (and_2_out, X[1], Y[1]);
  xor xor_3 (xor_3_out, X[2], Y[2]);
  and and_3 (and_3_out, X[2], Y[2]);
  xor xor_4 (xor_3_out, X[3], Y[3]);
  and and_4 (and_4_out, X[3], Y[3]);
  and and_5 (and_5_out, xor_1_out, in_5);
  and p2g1 (p2g1_out, xor_3_out, and_2_out);
  and and_6 (and_6_out, xor_3_out, and_3_out);
  or C1 (C1_out, and_1_out, and_5_out);
  or or_1 (or_1_out, and_5_out, and_1_out);
  and p1P2g0 (p1P2g0_out, xor_2_out, xor_3_out, and_1_out);
  and and_7 (and_7_out, xor_2_out, or_1_out);
  and P3P2G1 (P3P2G1_out, xor_3_out, xor_3_out, and_2_out);
  or C2 (C2_out, and_7_out, and_2_out);
  and and_8 (and_8_out, xor_2_out, xor_3_out, and_5_out);
  and and_9 (and_9_out, xor_2_out, and_1_out, xor_3_out, and_3_out);
  and and_10 (and_10_out, xor_3_out, and_5_out, xor_3_out, xor_2_out);
  or c3 (c3_out, p2g1_out, p1P2g0_out, and_8_out, and_3_out);
  or C4 (C4_out, and_4_out, and_6_out, P3P2G1_out, and_9_out, and_10_out);
  FULLADDER fulladder_3 (.X(in_2[1]), .Y(in_4[1]), .Cin(or_2_out), .SUM(out_9));
  FULLADDER fulladder_4 (.X(in_2[3]), .Y(in_4[3]), .Cin(or_5_out), .SUM(out_10));
  FULLADDER fulladder_5 (.X(in_2[0]), .Y(in_4[0]), .Cin(in_6), .SUM(out_12));
  FULLADDER fulladder_6 (.X(in_2[2]), .Y(in_4[2]), .Cin(or_4_out), .SUM(out_11));
  xor xor_5 (xor_5_out, in_2[0], in_4[0]);
  and and_11 (and_11_out, in_2[0], in_4[0]);
  xor xor_6 (xor_6_out, in_2[1], in_4[1]);
  and and_12 (and_12_out, in_2[1], in_4[1]);
  xor xor_7 (xor_7_out, in_2[2], in_4[2]);
  and and_13 (and_13_out, in_2[2], in_4[2]);
  xor xor_8 (xor_7_out, in_2[3], in_4[3]);
  and and_14 (and_14_out, in_2[3], in_4[3]);
  and and_15 (and_15_out, xor_5_out, in_6);
  and and_16 (and_16_out, xor_7_out, and_12_out);
  and and_17 (and_17_out, xor_7_out, and_13_out);
  or or_2 (or_2_out, and_11_out, and_15_out);
  or or_3 (or_3_out, and_15_out, and_11_out);
  and and_18 (and_18_out, xor_6_out, xor_7_out, and_11_out);
  and and_19 (and_19_out, xor_6_out, or_3_out);
  and and_20 (and_20_out, xor_7_out, xor_7_out, and_12_out);
  or or_4 (or_4_out, and_19_out, and_12_out);
  and and_21 (and_21_out, xor_6_out, xor_7_out, and_15_out);
  and and_22 (and_22_out, xor_6_out, and_11_out, xor_7_out, and_13_out);
  and and_23 (and_23_out, xor_7_out, and_15_out, xor_7_out, xor_6_out);
  or or_5 (or_5_out, and_16_out, and_18_out, and_21_out, and_13_out);
  or or_6 (out_13, and_14_out, and_17_out, and_20_out, and_22_out, and_23_out);

  // Notes on the sheet:
  //   P0
  //   G0
  //   P1
  //   G1
  //   P2
  //   G2
  //   P3
  //   G3
  //   P0C0
  //   P3G2
  //   P0
  //   G0
  //   P1
  //   G1
  //   P2
  //   G2
  //   P3
  //   G3
  //   P0C0
  //   P3G2
  //   C1
  //   P3P2G1
  //   C2
  //   P1P3G2G0
  //   P0P1P2P3C0
  //   C3
  //   C4
endmodule

module FULLADDER (
  input  X,
  input  Y,
  input  Cin,
  output SUM
);

  wire xor_1_out;

  xor xor_1 (xor_1_out, X, Y);
  xor xor_2 (SUM, xor_1_out, Cin);
endmodule
